# Fritzing sketch rp2350-wired-sed (saved by Fritzing 1.0.6)
breadboards: 1

parts:
  Mod1 = Raspberry Pi Pico
  Part1 = INMP441
  Pico-Audio1 = Waveshare Pico-Audio Pico 40pin [part_number=Pico-Audio]  # not connected
  Pico-LCD-1_1 = Waveshare Pico-LCD-1.3 Pico 40pin [part_number=Pico-LCD-1.3]  # not connected
  Sound_Event_D1 = Seeed Studio Sound Event Detection Module D1 [part_number="Sound Event Detection Module D1"]  # not connected

nets:
  N1: Mod1.pin_3, Mod1.pin_8, Mod1.pin_13, Mod1.pin_18, Mod1.pin_23, Mod1.pin_28, Mod1.pin_33, Mod1.pin_38, Mod1.pin_42, Part1.L/R, Part1.GND
  N2: Mod1.pin_21, Part1.SCK
  N3: Mod1.pin_26, Part1.WS
  N4: Mod1.pin_27, Part1.SD
  N5: Mod1.pin_39, Part1.VDD

custom parts:
  Raspberry Pi Pico: Raspberry Pi Pico. Based around the RP2040 microcontroller the Pico is a low cost microcontroller device bringing Raspberry Pi quality, cost, and easy of use to the microcontroller space. Jan 2021, Split part in to two versions: tht (this one) and SMD. This one will drill holes for a .1 in header in pcb to allow plugging in the module as well as providing pads to solder the module to the top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
  INMP441: This is a simple breakout board for the INMP441 I2S MEMS microphone.
  Waveshare Pico-Audio Pico 40pin: Approximate Fritzing part for Waveshare Pico-Audio. Connector mapping follows the Raspberry Pi Pico physical 40-pin header.
  Waveshare Pico-LCD-1.3 Pico 40pin: Approximate Fritzing part for Waveshare Pico-LCD-1.3. Connector mapping follows the Raspberry Pi Pico physical 40-pin header. LCD uses SPI0: DIN=GP11, CLK=GP10, CS=GP9, DC=GP8, RST=GP12, BL=GP13. Keys and joystick are labeled on related Pico GPIOs.
  Seeed Studio Sound Event Detection Module D1: Approximate Fritzing part for Seeed Studio Sound Event Detection Module D1. Breadboard and schematic expose the visible side pins 5V/GND/3V3/D10-D7 and D0-D6, plus auxiliary labeled pads INT/SDA/SCL/DOUT/IOP from the board silk. Verify against the actual board before PCB manufacturing.
